# Fritzing sketch 04_lcd_message_board (saved by Fritzing 0.9.2b)
breadboards: 1

parts:
  MonkMakesDuino1 = MonkMakesDuino
  U1 = LCD-16X2 [package=lcd-16x2_noholes]
  POT1 = Breadboard Trimpot

nets:
  N1: MonkMakesDuino1.3, U1.RS
  N2: MonkMakesDuino1.4, U1.E
  N3: MonkMakesDuino1.5, U1.DB4
  N4: MonkMakesDuino1.6, U1.DB5
  N5: MonkMakesDuino1.7, U1.DB6
  N6: MonkMakesDuino1.8, U1.DB7
  GND: MonkMakesDuino1.GND, U1.VSS, U1.R_W, U1.K, POT1.PIN3
  5V: MonkMakesDuino1.5V, U1.VDD, U1.A, POT1.PIN1
  N7: U1.VO, POT1.PIN2
