# Fritzing sketch 05_lcd_thermometer (saved by Fritzing 0.9.2b)
breadboards: 1

parts:
  MonkMakesDuino1 = MonkMakesDuino
  U1 = LCD-16X2 [package=lcd-16x2_noholes]
  POT1 = Breadboard Trimpot
  T1 = TMP36 Temperature Sensor [package="TO92 [THT]"]
  C1 = Electrolytic Capacitor [capacitance=100μF package="0807 [SMD, electrolytic]"]

nets:
  N1: MonkMakesDuino1.A3, T1.Vout
  N2: MonkMakesDuino1.3, U1.RS
  N3: MonkMakesDuino1.4, U1.E
  N4: MonkMakesDuino1.5, U1.DB4
  N5: MonkMakesDuino1.6, U1.DB5
  N6: MonkMakesDuino1.7, U1.DB6
  N7: MonkMakesDuino1.8, U1.DB7
  GND: MonkMakesDuino1.GND, U1.VSS, U1.R_W, U1.K, POT1.PIN3, T1.GND, C1.-
  5V: MonkMakesDuino1.5V, U1.VDD, U1.A, POT1.PIN1, T1.+Vs, C1.+
  N8: U1.VO, POT1.PIN2

notes:
  +
