# Fritzing sketch 06_timer (saved by Fritzing 0.9.2b)
breadboards: 1

parts:
  MonkMakesDuino1 = MonkMakesDuino
  U1 = LCD-16X2 [package=lcd-16x2_noholes]
  POT1 = Breadboard Trimpot
  S4 = Piezo Buzzer
  S3 = Pushbutton [package="[SMD]"]

nets:
  N1: MonkMakesDuino1.A2, S3.Pin_1
  N2: MonkMakesDuino1.3, U1.RS
  N3: MonkMakesDuino1.4, U1.E
  N4: MonkMakesDuino1.5, U1.DB4
  N5: MonkMakesDuino1.6, U1.DB5
  N6: MonkMakesDuino1.7, U1.DB6
  N7: MonkMakesDuino1.8, U1.DB7
  N8: MonkMakesDuino1.11, S4.pin2
  GND: MonkMakesDuino1.GND, U1.VSS, U1.R_W, U1.K, POT1.PIN3, S3.Pin_2
  5V: MonkMakesDuino1.5V, U1.VDD, U1.A, POT1.PIN1, S4.pin1
  N9: U1.VO, POT1.PIN2

custom parts:
  Piezo Buzzer: Piezo Buzzer (PCB Mount)
  Pushbutton: A generic pushbutton.
